# Fritzing sketch CircuitDiagram (saved by Fritzing 0.9.3b)
breadboards: 1

parts:
  hc-sr1 = hc-sr04  # not connected
  LED1 = LED - 3mm [color="Red (633nm)" package="3 mm [THT]"]
  LED2 = LED - 3mm [color="Red (633nm)" package="3 mm [THT]"]
  LED3 = LED - 3mm [color="Red (633nm)" package="3 mm [THT]"]
  T1 = LM35 Temperature Sensor [package="TO92 [THT]"]
  Componente2 = Arduino Uno (Rev3)
  R1 = Resistor [tolerance=±5% resistance=220 package=THT]
  R2 = Resistor [tolerance=±5% resistance=220 package=THT]
  R3 = Resistor [tolerance=±5% resistance=220 package=THT]

nets:
  N1: LED1.cathode, R3.Pin_0
  N2: LED1.anode, Componente2.D10_PWM/SS
  N3: LED2.cathode, R2.Pin_0
  N4: LED2.anode, Componente2.D12/MISO
  N5: LED3.cathode, R1.Pin_0
  N6: LED3.anode, Componente2.D13/SCK
  N7: T1.+Vs, Componente2.5V
  N8: T1.Vout, Componente2.A0
  GND: T1.GND, Componente2.GND, R1.Pin_1, R2.Pin_1, R3.Pin_1
